# Fritzing sketch Circuit (saved by Fritzing 0.9.3b)
breadboards: 1

parts:
  R4 = Resistor [tolerance=±0.1% resistance=2.2k package=THT]
  LCD1 = 2.8" SPI TFT Module [part_number=MSP2807]
  R3 = Resistor [tolerance=±0.1% resistance=2.2k package=THT]
  Bauteil1 = Arduino Mega ADK (Rev3)
  R1 = Resistor [tolerance=±0.1% resistance=2.2k package=THT]
  R5 = Resistor [tolerance=±0.1% resistance=2.2k package=THT]
  R2 = Resistor [tolerance=±0.1% resistance=2.2k package=THT]

nets:
  N1: R4.Pin_0, Bauteil1.D51/MOSI
  N2: R4.Pin_1, LCD1.pin6
  N3: LCD1.pin1, LCD1.pin8, Bauteil1.IOREF, Bauteil1.5V
  N4: LCD1.pin2, Bauteil1.GND
  N5: LCD1.pin3, R1.Pin_1
  N6: LCD1.pin4, R2.Pin_1
  N7: LCD1.pin5, R3.Pin_1
  N8: LCD1.pin7, R5.Pin_1
  N9: R3.Pin_0, Bauteil1.D49
  N10: Bauteil1.D47, R1.Pin_0
  N11: Bauteil1.D48, R2.Pin_0
  N12: Bauteil1.D52/SCK, R5.Pin_0

custom parts:
  2.8" SPI TFT Module: A generic 2.8 inch LCD TFT 320x240 display with touchscreen and SD card slot. Uses the ILI9341 controller, like the Adafruit displays of this size uses.
